// Logisim project Circuitos.circ as structural Verilog: 1 circuit, main circuit Compl_2
module Compl_2 (
  input  in_1,
  input  in_2,
  input  in_3,
  input  in_4,
  input  in_5,
  input  in_6,
  input  in_7,
  input  in_8,
  output out_9,
  output out_10,
  output out_11,
  output out_12,
  output out_13,
  output out_14,
  output out_15,
  output out_16
);

  wire adder_1_cout, adder_2_cout, adder_3_cout, adder_4_cout, adder_5_cout, adder_6_cout, adder_7_cout,
       adder_8_cout, not_1_out, not_2_out, not_3_out, not_4_out, not_5_out, not_6_out, not_7_out, not_8_out;

  not not_1 (not_1_out, in_1);
  Adder #(.width(1)) adder_1 (.a(not_1_out), .b(1'b0), .out(out_9), .cin(adder_2_cout), .cout(adder_1_cout));
  not not_2 (not_2_out, in_2);
  Adder #(.width(1)) adder_2 (.a(not_2_out), .b(1'b0), .out(out_10), .cin(adder_3_cout), .cout(adder_2_cout));
  not not_3 (not_3_out, in_3);
  Adder #(.width(1)) adder_3 (.a(not_3_out), .b(1'b0), .out(out_11), .cin(adder_4_cout), .cout(adder_3_cout));
  not not_4 (not_4_out, in_4);
  Adder #(.width(1)) adder_4 (.a(not_4_out), .b(1'b0), .out(out_12), .cin(adder_5_cout), .cout(adder_4_cout));
  not not_5 (not_5_out, in_5);
  Adder #(.width(1)) adder_5 (.a(not_5_out), .b(1'b0), .out(out_13), .cin(adder_6_cout), .cout(adder_5_cout));
  not not_6 (not_6_out, in_6);
  Adder #(.width(1)) adder_6 (.a(not_6_out), .b(1'b0), .out(out_14), .cin(adder_7_cout), .cout(adder_6_cout));
  not not_7 (not_7_out, in_7);
  Adder #(.width(1)) adder_7 (.a(not_7_out), .b(1'b0), .out(out_15), .cin(adder_8_cout), .cout(adder_7_cout));
  not not_8 (not_8_out, in_8);
  Adder #(.width(1)) adder_8 (.a(not_8_out), .b(1'b1), .out(out_16), .cin(1'b0), .cout(adder_8_cout));
endmodule
