// Logisim project AU.circ as structural Verilog: 1 circuit, main circuit AU
module AU (
  input  pi2,
  input  pi1,
  input  pi0,
  input  cih,
  input  cil,
  input  ch,
  input  cl,
  input  sh,
  input  sl,
  output rh,
  output rl
);

  wire and_1_out, and_2_out, and_3_out, and_4_out, and_5_out, and_6_out, and_7_out, and_8_out, and_9_out,
       and_10_out, and_11_out, and_12_out, and_13_out, and_14_out, and_15_out, and_16_out, and_17_out,
       and_18_out, and_19_out, and_20_out, and_21_out, and_22_out, not_1_out, not_2_out, not_3_out,
       not_4_out, not_5_out, not_6_out, not_7_out, not_8_out, not_9_out, not_10_out, or_1_out, or_2_out,
       or_3_out, or_4_out, or_5_out, or_6_out;

  not not_1 (not_1_out, pi1);
  not not_2 (not_2_out, pi0);
  not not_3 (not_3_out, pi1);
  not not_4 (not_4_out, pi1);
  not not_5 (not_5_out, pi0);
  not not_6 (not_6_out, pi1);
  and and_1 (and_1_out, not_1_out, not_2_out);
  and and_2 (and_2_out, not_3_out, pi0);
  not not_7 (not_7_out, pi0);
  not not_8 (not_8_out, pi2);
  and and_3 (and_3_out, not_4_out, not_5_out);
  and and_4 (and_4_out, not_6_out, pi0);
  not not_9 (not_9_out, pi0);
  not not_10 (not_10_out, pi2);
  and and_5 (and_5_out, and_1_out, cih);
  or or_1 (or_1_out, and_5_out, and_6_out);
  and and_6 (and_6_out, and_2_out, ch);
  and and_7 (and_7_out, pi1, not_7_out);
  and and_8 (and_8_out, and_7_out, ch);
  and and_9 (and_9_out, not_8_out, pi1);
  and and_10 (and_10_out, and_9_out, and_11_out);
  and and_11 (and_11_out, pi0, cih);
  and and_12 (and_12_out, pi2, pi1);
  and and_13 (and_13_out, and_12_out, ch);
  and and_14 (and_14_out, and_3_out, cil);
  or or_2 (or_2_out, and_14_out, and_15_out);
  and and_15 (and_15_out, and_4_out, cl);
  and and_16 (and_16_out, pi1, not_9_out);
  and and_17 (and_17_out, and_16_out, cl);
  and and_18 (and_18_out, not_10_out, pi1);
  and and_19 (and_19_out, and_18_out, and_20_out);
  and and_20 (and_20_out, pi0, cil);
  and and_21 (and_21_out, pi2, pi1);
  and and_22 (and_22_out, and_21_out, cl);
  or or_3 (or_3_out, or_1_out, and_8_out);
  or or_4 (or_4_out, and_10_out, and_13_out);
  or or_5 (or_5_out, or_2_out, and_17_out);
  or or_6 (or_6_out, and_19_out, and_22_out);
  or or_7 (rh, or_3_out, or_4_out);
  or or_8 (rl, or_5_out, or_6_out);
endmodule
