// Logisim project Parcial.circ as structural Verilog: 2 circuits, main circuit P4
module P4 (
  input  A,
  input  B,
  input  C,
  output Y,
  output Z
);

  wire and_1_out, and_2_out, and_3_out, and_4_out, and_5_out, and_6_out, and_7_out, and_8_out, and_9_out,
       not_1_out, not_2_out, not_3_out, not_4_out, not_5_out, not_6_out, or_2_out, or_3_out;

  not not_1 (not_1_out, B);
  not not_2 (not_2_out, B);
  and and_1 (and_1_out, A, not_1_out);
  and and_2 (and_2_out, A, B);
  not not_3 (not_3_out, C);
  not not_4 (not_4_out, A);
  not not_5 (not_5_out, A);
  and and_3 (and_3_out, A, not_2_out);
  not not_6 (not_6_out, C);
  and and_4 (and_4_out, and_1_out, C);
  and and_5 (and_5_out, and_2_out, not_3_out);
  and and_6 (and_6_out, not_4_out, C);
  and and_7 (and_7_out, not_5_out, B);
  and and_8 (and_8_out, B, C);
  and and_9 (and_9_out, and_3_out, not_6_out);
  or or_1 (Y, and_4_out, and_5_out);
  or or_2 (or_2_out, and_6_out, and_7_out);
  or or_3 (or_3_out, and_8_out, and_9_out);
  or or_4 (Z, or_2_out, or_3_out);
endmodule

module p3 (
  input  A,
  input  B,
  input  C,
  output Y,
  output Z
);

  wire and_1_out, not_1_out;

  not not_1 (not_1_out, A);
  and and_1 (and_1_out, B, C);
  xor xor_1 (Y, not_1_out, and_1_out);
  or or_1 (Z, and_1_out, C);
endmodule
