// Logisim project quiz7.circ as structural Verilog
module p2 (
  input  x,
  input  y,
  input  z,
  output s
);

  wire and_1_out, and_2_out, and_3_out, and_4_out, not_1_out, not_2_out, not_3_out, not_4_out, or_1_out,
       or_2_out;

  not not_1 (not_1_out, x);
  not not_2 (not_2_out, x);
  not not_3 (not_3_out, y);
  not not_4 (not_4_out, z);
  and and_1 (and_1_out, not_1_out, z);
  and and_2 (and_2_out, not_2_out, y);
  and and_3 (and_3_out, x, not_3_out);
  and and_4 (and_4_out, x, not_4_out);
  or or_1 (or_1_out, and_1_out, and_2_out);
  or or_2 (or_2_out, and_3_out, and_4_out);
  or or_3 (s, or_1_out, or_2_out);
endmodule

module p1 (
  input  a,
  input  b,
  input  c,
  input  d,
  input  e,
  output s
);

  wire and_1_out, and_2_out, and_3_out, and_4_out, or_1_out, or_2_out;

  and and_1 (and_1_out, d, e);
  and and_2 (and_2_out, c, d);
  and and_3 (and_3_out, b, c);
  and and_4 (and_4_out, a, b);
  or or_1 (or_1_out, and_1_out, and_2_out);
  or or_2 (or_2_out, and_3_out, and_4_out);
  or or_3 (s, or_1_out, or_2_out);
endmodule

module p3 (
  input  a,
  input  b,
  input  c,
  output s
);


  assign s = c;
endmodule
